// Logisim project CU.circ as structural Verilog: 1 circuit, main circuit main
module main (
  input  [7:0] in_1,
  output [3:0] Address,
  output Stop,
  output out_4,
  output Add,
  output Sub,
  output Beq,
  output Bnq,
  output Ld1,
  output Ld2,
  output Str1,
  output Str2,
  output Prt,
  output Inp
);

  Decoder #(.select(4), .enable("false")) decoder_1 (
    .out0(Stop), .out1(out_4), .out2(Add), .out3(Sub), .out4(Beq), .out5(Bnq), .out6(Ld1), .out7(Ld2),
    .out8(Str1), .out9(Str2), .out10(Prt), .out11(Inp), .sel(in_1[7:4]));  // open: out12, out13, out14, out15

  assign Address = in_1[3:0];
endmodule
